# Fritzing sketch iohannes (saved by Fritzing 0.7.4b)

parts:
  HC-SR04 = HC-SR04 Ultrasonic Rangefinder
  SparkFun_IOIO = IOIO for Android
  RKI-1004 = Generic Motor Driver
  9V_1800mAH = Power plug
  M1 = DC Motor
  M2 = DC Motor
  12V_2200mAH = Power plug

nets:
  N1: HC-SR04.no_name_yet#8, SparkFun_IOIO.5V
  N2: HC-SR04.no_name_yet#9, SparkFun_IOIO.PIN2
  N3: HC-SR04.no_name_yet#10, SparkFun_IOIO.PIN7
  GND: HC-SR04.no_name_yet#11, SparkFun_IOIO.GND, 9V_1800mAH.GND
  VCC: SparkFun_IOIO.VCC, 9V_1800mAH.VCC
  N4: RKI-1004.no_name_yet#141, M2.pin_2
  N5: RKI-1004.no_name_yet#144, M1.pin_2
  N6: RKI-1004.connector152, 12V_2200mAH.VCC
  N7: RKI-1004.connector154, 12V_2200mAH.GND
  N8: RKI-1004.connector155, M1.pin_1
  N9: RKI-1004.connector156, M2.pin_1
